// Logisim project Lab2.1.circ as structural Verilog: 1 circuit, main circuit main
module main (
  input  [7:0] X,
  input  [7:0] Y,
  input  [7:0] Z,
  output [7:0] X___Y___Z,
  output [7:0] XY___XZ,
  output [7:0] X___YZ,
  output [7:0] out_7
);

  wire [7:0] X___Y_out, X___Z_out, XY_out, XZ_out, Y___Z_out, YZ_out;

  assign Y___Z_out = Y | Z;  // OR_Gate Y___Z, 8 bits wide
  assign X___Y___Z = X & Y___Z_out;  // AND_Gate and_1, 8 bits wide
  assign XY_out = X & Y;  // AND_Gate XY, 8 bits wide
  assign XZ_out = X & Z;  // AND_Gate XZ, 8 bits wide
  assign XY___XZ = XY_out | XZ_out;  // OR_Gate or_1, 8 bits wide
  assign YZ_out = Y & Z;  // AND_Gate YZ, 8 bits wide
  assign X___YZ = X | YZ_out;  // OR_Gate or_2, 8 bits wide
  assign X___Y_out = X | Y;  // OR_Gate X___Y, 8 bits wide
  assign X___Z_out = X | Z;  // OR_Gate X___Z, 8 bits wide
  assign out_7 = X___Y_out & X___Z_out;  // AND_Gate and_2, 8 bits wide

  // Notes on the sheet:
  //   ( X + Y ) ( X + Z )
endmodule
