// Logisim project Lab2.2.circ as structural Verilog: 1 circuit, main circuit main
module main (
  input  [7:0] X,
  input  [7:0] Y,
  input  [7:0] Z,
  output [7:0] X___Y___Z__prime,
  output [7:0] out_5,
  output [7:0] X_prime___Y_prime___Z_prime,
  output [7:0] XYZ__prime
);

  wire [7:0] not_1_out, not_2_out, not_3_out;

  assign X___Y___Z__prime = ~(X | Y | Z);  // NOR_Gate nor_1, 8 bits wide
  assign not_1_out = ~X;  // NOT_Gate not_1, 8 bits wide
  assign not_2_out = ~Y;  // NOT_Gate not_2, 8 bits wide
  assign not_3_out = ~Z;  // NOT_Gate not_3, 8 bits wide
  assign out_5 = not_1_out & not_2_out & not_3_out;  // AND_Gate and_1, 8 bits wide
  assign X_prime___Y_prime___Z_prime = not_1_out | not_2_out | not_3_out;  // OR_Gate or_1, 8 bits wide
  assign XYZ__prime = ~(X & Y & Z);  // NAND_Gate nand_1, 8 bits wide

  // Notes on the sheet:
  //   X'Y'Z'
endmodule
