// Logisim project Lab2.3.circ as structural Verilog: 1 circuit, main circuit main
module main (
  input  [3:0] X,
  input  [3:0] Y,
  output [3:0] out_3,
  output [3:0] out_4
);

  wire [3:0] not_1_out, not_2_out, X___Y_out, X_prime___Y_prime_out, X_prime_Y_prime_out, XY_out;

  assign not_1_out = ~X;  // NOT_Gate not_1, 4 bits wide
  assign not_2_out = ~Y;  // NOT_Gate not_2, 4 bits wide
  assign XY_out = X & Y;  // AND_Gate XY, 4 bits wide
  assign X_prime___Y_prime_out = not_1_out | not_2_out;  // OR_Gate X_prime___Y_prime, 4 bits wide
  assign out_3 = X_prime___Y_prime_out | XY_out;  // OR_Gate or_1, 4 bits wide
  assign X_prime_Y_prime_out = not_1_out & not_2_out;  // AND_Gate X_prime_Y_prime, 4 bits wide
  assign X___Y_out = X | Y;  // OR_Gate X___Y, 4 bits wide
  assign out_4 = X___Y_out & X_prime_Y_prime_out;  // AND_Gate and_1, 4 bits wide

  // Notes on the sheet:
  //   ( X ' + Y ' ) + X Y
  //   ( X ' Y ' ) ( X + Y )
endmodule
