// Logisim project Lab3A.circ as structural Verilog: 1 circuit, main circuit main
module main (
  input  [15:0] W,
  input  [15:0] X,
  input  [15:0] Y,
  input  [15:0] Z,
  output [15:0] out_5
);

  wire [15:0] nand_1_out, nand_2_out, nand_3_out, nand_4_out, nand_5_out, nand_6_out, nand_7_out, nand_8_out,
       nand_9_out, nand_10_out, nand_11_out, nand_12_out, nand_13_out, nand_14_out, nand_15_out;

  assign nand_1_out = ~(W & W);  // NAND_Gate nand_1, 16 bits wide
  assign nand_2_out = ~(X & X);  // NAND_Gate nand_2, 16 bits wide
  assign nand_3_out = ~(Y & Y);  // NAND_Gate nand_3, 16 bits wide
  assign nand_4_out = ~(Z & Z);  // NAND_Gate nand_4, 16 bits wide
  assign nand_5_out = ~(nand_2_out & Y & nand_1_out & Z);  // NAND_Gate nand_5, 16 bits wide
  assign nand_6_out = ~(W & nand_2_out & Y & nand_4_out);  // NAND_Gate nand_6, 16 bits wide
  assign nand_7_out = ~(Y & nand_1_out & nand_4_out & X);  // NAND_Gate nand_7, 16 bits wide
  assign nand_8_out = ~(X & W & nand_4_out & nand_3_out);  // NAND_Gate nand_8, 16 bits wide
  assign nand_9_out = ~(W & nand_2_out & nand_3_out & Z);  // NAND_Gate nand_9, 16 bits wide
  assign nand_10_out = ~(nand_1_out & X & nand_3_out & Z);  // NAND_Gate nand_10, 16 bits wide
  assign nand_11_out = ~(nand_5_out & nand_6_out & nand_7_out);  // NAND_Gate nand_11, 16 bits wide
  assign nand_12_out = ~(nand_8_out & nand_9_out & nand_10_out);  // NAND_Gate nand_12, 16 bits wide
  assign nand_13_out = ~(nand_11_out & nand_11_out);  // NAND_Gate nand_13, 16 bits wide
  assign nand_14_out = ~(nand_12_out & nand_12_out);  // NAND_Gate nand_14, 16 bits wide
  assign nand_15_out = ~(nand_13_out & nand_14_out);  // NAND_Gate nand_15, 16 bits wide
  assign out_5 = ~(nand_15_out & nand_15_out);  // NAND_Gate nand_16, 16 bits wide
endmodule
