// Logisim project Lab3B.circ as structural Verilog: 1 circuit, main circuit main
module main (
  input  [15:0] W,
  input  [15:0] X,
  input  [15:0] Y,
  input  [15:0] Z,
  output [15:0] out_5
);

  wire [15:0] xor_1_out, xor_2_out;

  assign xor_1_out = W ^ X;  // XOR_Gate xor_1, 16 bits wide
  assign xor_2_out = Y ^ Z;  // XOR_Gate xor_2, 16 bits wide
  assign out_5 = xor_1_out ^ xor_2_out;  // XOR_Gate xor_3, 16 bits wide
endmodule
