// Logisim project Lab3C.circ as structural Verilog: 1 circuit, main circuit main
module main (
  input  W,
  input  X,
  input  Y,
  input  Z
);

  wire and_1_out, and_2_out, and_3_out, and_4_out, and_5_out, and_6_out, and_7_out, and_8_out, and_9_out,
       and_10_out, and_11_out, and_12_out, and_13_out, not_1_out, not_2_out, not_3_out, not_4_out, or_1_out,
       or_2_out, or_3_out, or_4_out, or_5_out, or_6_out;

  not not_1 (not_1_out, W);
  not not_2 (not_2_out, X);
  not not_3 (not_3_out, Y);
  not not_4 (not_4_out, Z);
  and and_1 (and_1_out, not_4_out, not_3_out);
  and and_2 (and_2_out, Z, X);
  and and_3 (and_3_out, not_1_out, not_2_out);
  or or_1 (or_1_out, W, X, Y);
  and and_4 (and_4_out, Y, not_4_out);
  and and_5 (and_5_out, not_1_out, not_2_out);
  and and_6 (and_6_out, not_1_out, Z);
  and and_7 (and_7_out, not_4_out, not_3_out);
  and and_8 (and_8_out, not_1_out, Z);
  and and_9 (and_9_out, not_2_out, Z);
  and and_10 (and_10_out, not_1_out, not_3_out);
  and and_11 (and_11_out, not_3_out, not_4_out);
  and and_12 (and_12_out, not_2_out, Z);
  and and_13 (and_13_out, Y, Z);
  or or_2 (or_2_out, and_1_out, and_3_out, and_2_out);
  or or_3 (or_3_out, W, not_3_out, and_5_out, and_4_out);
  or or_4 (or_4_out, and_7_out, and_6_out);
  or or_5 (or_5_out, and_9_out, and_10_out);
  or or_6 (or_6_out, and_11_out, and_12_out, and_13_out);
  _7_Segment_Display u_7_segment_display_1 (
    .g(or_6_out), .f(or_5_out), .a(or_2_out), .b(or_1_out), .e(and_8_out), .d(or_4_out), .c(or_3_out));  // open: dp
endmodule
