// Logisim project Lab4.circ as structural Verilog: 4 circuits, main circuit main
module main (
  input  [3:0] X,
  input  [3:0] Y,
  input  [7:0] X_2,
  input  [7:0] Y_2,
  input  [7:0] Z,
  input  A2,
  input  A1,
  input  A0,
  input  B2,
  input  B1,
  input  B0,
  input  C0,
  input  [3:0] Y_3,
  input  [3:0] Z_2,
  input  [1:0] W_X_SEL,
  input  Enabler,
  input  [1:0] Z_3,
  input  [1:0] O,
  input  [2:0] W__X__Y__SEL,
  input  Enabler_2,
  input  C0_2,
  input  X4,
  input  X3,
  input  X2,
  input  X1,
  input  X0,
  input  Y4,
  input  Y3,
  input  Y2,
  input  Y1,
  input  Y0,
  output [3:0] S,
  output [3:0] C,
  output [7:0] S_2,
  output [7:0] C_2,
  output S2,
  output C3,
  output S1,
  output S0,
  output [3:0] F,
  output [1:0] F_2,
  output S0_2,
  output S1_2,
  output S2_2,
  output S3,
  output S4,
  output OF
);

  wire full_adder_2_c, full_adder_3_c;
  wire [1:0] not_3_out;
  wire [3:0] and_4_out, and_5_out, and_6_out, not_1_out, not_2_out, or_2_out;
  wire [7:0] and_2_out, and_3_out, xor_2_out;

  assign C = X & Y;  // AND_Gate and_1, 4 bits wide
  Full_Adder full_adder_1 (.X(A2), .Y(B2), .Z(full_adder_2_c), .S(S2), .C(C3));
  Full_Adder full_adder_2 (.X(A1), .Y(B1), .Z(full_adder_3_c), .S(S1), .C(full_adder_2_c));
  Full_Adder full_adder_3 (.X(A0), .Y(B0), .Z(C0), .S(S0), .C(full_adder_3_c));
  EC ec_1 (
    .C0(C0_2), .X4(X4), .X3(X3), .X2(X2), .X1(X1), .X0(X0), .Y4(Y4), .Y3(Y3), .Y2(Y2), .Y1(Y1), .Y0(Y0),
    .S0(S0_2), .S1(S1_2), .S2(S2_2), .S3(S3), .S4(S4), .OF(OF));
  assign S = X ^ Y;  // XOR_Gate xor_1, 4 bits wide
  assign xor_2_out = X_2 ^ Y_2;  // XOR_Gate xor_2, 8 bits wide
  assign and_2_out = X_2 & Y_2;  // AND_Gate and_2, 8 bits wide
  assign not_1_out = ~Y_3;  // NOT_Gate not_1, 4 bits wide
  assign not_2_out = ~Z_2;  // NOT_Gate not_2, 4 bits wide
  assign S_2 = xor_2_out ^ Z;  // XOR_Gate xor_3, 8 bits wide
  assign and_3_out = Z & xor_2_out;  // AND_Gate and_3, 8 bits wide
  assign and_4_out = Y_3 & Z_2;  // AND_Gate and_4, 4 bits wide
  assign and_5_out = not_1_out & not_2_out;  // AND_Gate and_5, 4 bits wide
  assign and_6_out = Y_3 & not_2_out;  // AND_Gate and_6, 4 bits wide
  assign not_3_out = ~Z_3;  // NOT_Gate not_3, 2 bits wide
  Multiplexer #(.select(3), .width(2)) multiplexer_1 (
    .in0(not_3_out), .in1(Z_3), .in2(Z_3), .in3(Z_3), .in4(not_3_out), .in5(Z_3), .in6(O), .in7(not_3_out),
    .out(F_2), .sel(W__X__Y__SEL), .en(Enabler_2));
  assign C_2 = and_2_out | and_3_out;  // OR_Gate or_1, 8 bits wide
  assign or_2_out = and_4_out | and_5_out;  // OR_Gate or_2, 4 bits wide
  Multiplexer #(.select(2), .width(4)) multiplexer_2 (
    .in0(or_2_out), .in1(Z_2), .in2(or_2_out), .in3(and_6_out), .out(F), .en(Enabler));  // open: sel
endmodule

module Half_Adder (
  input  X,
  input  Y,
  output S,
  output C
);

  xor xor_1 (S, X, Y);
  and and_1 (C, X, Y);
endmodule

module Full_Adder (
  input  X,
  input  Y,
  input  Z,
  output S,
  output C
);

  wire and_1_out, and_2_out, xor_1_out;

  xor xor_1 (xor_1_out, X, Y);
  and and_1 (and_1_out, X, Y);
  xor xor_2 (S, xor_1_out, Z);
  and and_2 (and_2_out, Z, xor_1_out);
  or or_1 (C, and_1_out, and_2_out);
endmodule

// EC Circuit
module EC (
  input  C0,
  input  X4,
  input  X3,
  input  X2,
  input  X1,
  input  X0,
  input  Y4,
  input  Y3,
  input  Y2,
  input  Y1,
  input  Y0,
  output S0,
  output S1,
  output S2,
  output S3,
  output S4,
  output OF
);

  wire FA0_c, FA1_c, FA2_c, FA3_c, FA4_c;

  Full_Adder FA0 (.X(X0), .Y(Y0), .Z(C0), .S(S0), .C(FA0_c));
  Full_Adder FA1 (.X(X1), .Y(Y1), .Z(FA0_c), .S(S1), .C(FA1_c));
  Full_Adder FA2 (.X(X2), .Y(Y2), .Z(FA1_c), .S(S2), .C(FA2_c));
  Full_Adder FA3 (.X(X3), .Y(Y3), .Z(FA2_c), .S(S3), .C(FA3_c));
  Full_Adder FA4 (.X(X4), .Y(Y4), .Z(FA3_c), .S(S4), .C(FA4_c));
  xor xor_1 (OF, FA4_c, FA3_c);
endmodule
