// Logisim project Lab4Part1.circ as structural Verilog: 3 circuits, main circuit main
module main (
  input  [3:0] X,
  input  [3:0] Y,
  input  [7:0] X_2,
  input  [7:0] Y_2,
  input  [7:0] Z,
  input  A2,
  input  A1,
  input  A0,
  input  B2,
  input  B1,
  input  B0,
  input  C0,
  output [3:0] S,
  output [3:0] C,
  output [7:0] S_2,
  output [7:0] C_2,
  output S2,
  output C3,
  output S1,
  output S0
);

  wire full_adder_2_c, full_adder_3_c;
  wire [7:0] and_2_out, and_3_out, xor_2_out;

  assign C = X & Y;  // AND_Gate and_1, 4 bits wide
  Full_Adder full_adder_1 (.X(A2), .Y(B2), .Z(full_adder_2_c), .S(S2), .C(C3));
  Full_Adder full_adder_2 (.X(A1), .Y(B1), .Z(full_adder_3_c), .S(S1), .C(full_adder_2_c));
  Full_Adder full_adder_3 (.X(A0), .Y(B0), .Z(C0), .S(S0), .C(full_adder_3_c));
  assign S = X ^ Y;  // XOR_Gate xor_1, 4 bits wide
  assign xor_2_out = X_2 ^ Y_2;  // XOR_Gate xor_2, 8 bits wide
  assign and_2_out = X_2 & Y_2;  // AND_Gate and_2, 8 bits wide
  assign S_2 = xor_2_out ^ Z;  // XOR_Gate xor_3, 8 bits wide
  assign and_3_out = Z & xor_2_out;  // AND_Gate and_3, 8 bits wide
  assign C_2 = and_2_out | and_3_out;  // OR_Gate or_1, 8 bits wide
endmodule

module Half_Adder (
  input  X,
  input  Y,
  output S,
  output C
);

  xor xor_1 (S, X, Y);
  and and_1 (C, X, Y);
endmodule

module Full_Adder (
  input  X,
  input  Y,
  input  Z,
  output S,
  output C
);

  wire and_1_out, and_2_out, xor_1_out;

  xor xor_1 (xor_1_out, X, Y);
  and and_1 (and_1_out, X, Y);
  xor xor_2 (S, xor_1_out, Z);
  and and_2 (and_2_out, Z, xor_1_out);
  or or_1 (C, and_1_out, and_2_out);
endmodule
