// Logisim project Lab4Part2.circ as structural Verilog: 4 circuits, main circuit main
module main (
  input  [3:0] Y,
  input  [3:0] Z,
  input  [1:0] W_X_SEL,
  input  Enabler,
  output [3:0] F
);

  wire [3:0] and_1_out, and_2_out, and_3_out, not_1_out, not_2_out, or_1_out;

  assign not_1_out = ~Y;  // NOT_Gate not_1, 4 bits wide
  assign not_2_out = ~Z;  // NOT_Gate not_2, 4 bits wide
  assign and_1_out = Y & Z;  // AND_Gate and_1, 4 bits wide
  assign and_2_out = not_1_out & not_2_out;  // AND_Gate and_2, 4 bits wide
  assign and_3_out = Y & not_2_out;  // AND_Gate and_3, 4 bits wide
  assign or_1_out = and_1_out | and_2_out;  // OR_Gate or_1, 4 bits wide
  Multiplexer #(.select(2), .width(4)) multiplexer_1 (
    .in0(or_1_out), .in1(Z), .in2(or_1_out), .in3(and_3_out), .out(F), .sel(W_X_SEL), .en(Enabler));
endmodule

module Half_Adder (
  input  X,
  input  Y,
  output S,
  output C
);

  xor xor_1 (S, X, Y);
  and and_1 (C, X, Y);
endmodule

module Full_Adder (
  input  X,
  input  Y,
  input  Z,
  output S,
  output C
);

  wire and_1_out, and_2_out, xor_1_out;

  xor xor_1 (xor_1_out, X, Y);
  and and_1 (and_1_out, X, Y);
  xor xor_2 (S, xor_1_out, Z);
  and and_2 (and_2_out, Z, xor_1_out);
  or or_1 (C, and_1_out, and_2_out);
endmodule

// EC Circuit
module EC (
  input  C0,
  input  X4,
  input  X3,
  input  X2,
  input  X1,
  input  X0,
  input  Y4,
  input  Y3,
  input  Y2,
  input  Y1,
  input  Y0,
  output S0,
  output S1,
  output S2,
  output S3,
  output S4,
  output OF
);

  wire FA0_c, FA1_c, FA2_c, FA3_c, FA4_c;

  Full_Adder FA0 (.X(X0), .Y(Y0), .Z(C0), .S(S0), .C(FA0_c));
  Full_Adder FA1 (.X(X1), .Y(Y1), .Z(FA0_c), .S(S1), .C(FA1_c));
  Full_Adder FA2 (.X(X2), .Y(Y2), .Z(FA1_c), .S(S2), .C(FA2_c));
  Full_Adder FA3 (.X(X3), .Y(Y3), .Z(FA2_c), .S(S3), .C(FA3_c));
  Full_Adder FA4 (.X(X4), .Y(Y4), .Z(FA3_c), .S(S4), .C(FA4_c));
  xor xor_1 (OF, FA4_c, FA3_c);
endmodule
