// Logisim project Lab4Part3.circ as structural Verilog: 4 circuits, main circuit main
module main (
  input  [1:0] Z,
  input  [1:0] O,
  input  [2:0] W__X__Y__SEL,
  input  Enabler,
  input  C0,
  input  X4,
  input  X3,
  input  X2,
  input  X1,
  input  X0,
  input  Y4,
  input  Y3,
  input  Y2,
  input  Y1,
  input  Y0,
  output [1:0] F,
  output S0,
  output S1,
  output S2,
  output S3,
  output S4,
  output OF
);

  wire [1:0] not_1_out;

  EC ec_1 (
    .C0(C0), .X4(X4), .X3(X3), .X2(X2), .X1(X1), .X0(X0), .Y4(Y4), .Y3(Y3), .Y2(Y2), .Y1(Y1), .Y0(Y0),
    .S0(S0), .S1(S1), .S2(S2), .S3(S3), .S4(S4), .OF(OF));
  assign not_1_out = ~Z;  // NOT_Gate not_1, 2 bits wide
  Multiplexer #(.select(3), .width(2)) multiplexer_1 (
    .in0(not_1_out), .in1(Z), .in2(Z), .in3(Z), .in4(not_1_out), .in5(Z), .in6(O), .in7(not_1_out), .out(F),
    .sel(W__X__Y__SEL), .en(Enabler));
endmodule

module Half_Adder (
  input  X,
  input  Y,
  output S,
  output C
);

  xor xor_1 (S, X, Y);
  and and_1 (C, X, Y);
endmodule

module Full_Adder (
  input  X,
  input  Y,
  input  Z,
  output S,
  output C
);

  wire and_1_out, and_2_out, xor_1_out;

  xor xor_1 (xor_1_out, X, Y);
  and and_1 (and_1_out, X, Y);
  xor xor_2 (S, xor_1_out, Z);
  and and_2 (and_2_out, Z, xor_1_out);
  or or_1 (C, and_1_out, and_2_out);
endmodule

// EC Circuit
module EC (
  input  C0,
  input  X4,
  input  X3,
  input  X2,
  input  X1,
  input  X0,
  input  Y4,
  input  Y3,
  input  Y2,
  input  Y1,
  input  Y0,
  output S0,
  output S1,
  output S2,
  output S3,
  output S4,
  output OF
);

  wire FA0_c, FA1_c, FA2_c, FA3_c, FA4_c;

  Full_Adder FA0 (.X(X0), .Y(Y0), .Z(C0), .S(S0), .C(FA0_c));
  Full_Adder FA1 (.X(X1), .Y(Y1), .Z(FA0_c), .S(S1), .C(FA1_c));
  Full_Adder FA2 (.X(X2), .Y(Y2), .Z(FA1_c), .S(S2), .C(FA2_c));
  Full_Adder FA3 (.X(X3), .Y(Y3), .Z(FA2_c), .S(S3), .C(FA3_c));
  Full_Adder FA4 (.X(X4), .Y(Y4), .Z(FA3_c), .S(S4), .C(FA4_c));
  xor xor_1 (OF, FA4_c, FA3_c);
endmodule
